# Fritzing sketch NOP (saved by Fritzing 1.0.4)
breadboards: 1

parts:
  6309 = HD63C09 [package="DIP (Dual Inline) [THT]"]
  R1 = Resistor [tolerance=±1% power=0.25W resistance=4.7k package=THT]
  R2 = Resistor [tolerance=±1% power=0.25W resistance=4.7k package=THT]
  R3 = Resistor [tolerance=±1% power=0.25W resistance=4.7k package=THT]
  D1 = LED_BARGRAPH_10 [package=led_bargaph_10]
  D2 = LED_BARGRAPH_10 [package=led_bargaph_10]  # not connected

nets:
  N1: 6309./NMI, R1.Pin_1
  N2: 6309./IRQ, R2.Pin_1
  N3: 6309./FIRQ, R3.Pin_1
  N4: 6309.VCC, R1.Pin_0, R2.Pin_0, R3.Pin_0
  N5: 6309.A0, D1.A_A
  N6: 6309.A1, D1.B_A
  N7: 6309.A2, D1.C_A

custom parts:
  HD63C09: 8-bit microprocessor, compatible with the MC6809
